# Fritzing sketch layout 2 (saved by Fritzing 0.9.4)
circuit board: 8cm x 6cm
breadboards: 1

parts:
  C1 = Electrolytic Capacitor [capacitance=10µF voltage=50V package="100 mil [THT, electrolytic]"]
  C2 = Electrolytic Capacitor [capacitance=0.1mF voltage=50V package="100 mil [THT, electrolytic]"]
  Power_12v = Power plug [part_number=12v]
  Heltec_WiFi_LoRa_32 = Heltec WiFi LoRa 32 V2 [part_number=HTIT-WB32LA]
  C3 = Ceramic Capacitor [capacitance=30nF voltage=50V package="100 mil [THT, multilayer]"]
  7805 = Voltage Regulator - 5V [package="TO220 [THT]"]
  R1 = Resistor [tolerance=±1% resistance=10k package=THT]
  ENCODER1 = Rotary Encoder with switch (KY-040) [part_number=KY-040]  # not connected
  rotary = screw terminal, 5 pins
  5v = Screw terminal - 2 pins [package=THT]
  Driver_Motor = screw terminal, 4 pins
  IRLZ44N = MOSFET-NCHANNEL [package=to220v]
  switch = Toggle Switch [package=THT]
  3v3_32_33 = screw terminal, 3 pins
  tira_de_leds = Camdenboss CTB0158-3 [part_number=CTB0158-3 package=THT]

nets:
  GND: C1.-, C2.-, Power_12v.GND, Heltec_WiFi_LoRa_32.pin_18, Heltec_WiFi_LoRa_32.pin_19, C3.0, 7805.GND, R1.Pin_1, rotary.pin1, 5v.pin2, IRLZ44N.S, tira_de_leds.pin3
  N1: C1.+, C3.1, 7805.output_voltage, switch.L2
  N2: C2.+, Power_12v.VCC, 7805.input_voltage, tira_de_leds.pin2
  N3: Heltec_WiFi_LoRa_32.pin_1, Driver_Motor.pin4
  N4: Heltec_WiFi_LoRa_32.pin_2, Driver_Motor.pin3
  N5: Heltec_WiFi_LoRa_32.pin_3, Driver_Motor.pin2
  N6: Heltec_WiFi_LoRa_32.pin_4, Driver_Motor.pin1
  N7: Heltec_WiFi_LoRa_32.pin_7, R1.Pin_0, IRLZ44N.G
  N8: Heltec_WiFi_LoRa_32.pin_8, 3v3_32_33.pin3
  N9: Heltec_WiFi_LoRa_32.pin_9, 3v3_32_33.pin2
  N10: Heltec_WiFi_LoRa_32.pin_16, rotary.pin2, 3v3_32_33.pin1
  N11: Heltec_WiFi_LoRa_32.pin_20, 5v.pin1, switch.COM
  N12: Heltec_WiFi_LoRa_32.pin_29, rotary.pin5
  N13: Heltec_WiFi_LoRa_32.pin_30, rotary.pin4
  N14: Heltec_WiFi_LoRa_32.pin_35, rotary.pin3
  N15: IRLZ44N.D, tira_de_leds.pin1

notes:
  -  + gnd
  -+

custom parts:
  Heltec WiFi LoRa 32 V2: Heltec WiFi LoRa 32 V2 WiFi LoRa 32 is a classic IoT dev-board designed & produced by Heltec Automation(TM). It’s a highly integrated product based on ESP32 + SX127x, it has Wi-Fi, BLE, LoRa functions, also Li-Po battery management system, 0.96″ OLED are also included. It’s the best choice for smart cities, smart farms, smart home, and IoT makers.
  Rotary Encoder with switch (KY-040): A Rotary Encoder with switch
