# Fritzing sketch layout (saved by Fritzing 0.9.4)
circuit board: 8cm x 4.4cm
breadboards: 1

parts:
  C1 = Electrolytic Capacitor [capacitance=10µF voltage=50V package="100 mil [THT, electrolytic]"]
  C2 = Electrolytic Capacitor [capacitance=0.1mF voltage=50V package="100 mil [THT, electrolytic]"]
  Power_12v = Power plug [part_number=12v]
  Heltec_WiFi_LoRa_32 = Heltec WiFi LoRa 32 V2 [part_number=HTIT-WB32LA]
  C3 = Ceramic Capacitor [capacitance=100nF voltage=50V package="100 mil [THT, multilayer]"]
  7805 = Voltage Regulator - 5V [package="TO220 [THT]"]
  tira_de_leds = Camdenboss CTB0158-2 [package=THT]
  R1 = Resistor [tolerance=±1% resistance=10k package=THT]
  ENCODER1 = Rotary Encoder with switch (KY-040) [part_number=KY-040]  # not connected
  rotary = screw terminal, 5 pins
  12v = Screw terminal - 2 pins [package=THT]
  Driver_Motor = screw terminal, 4 pins
  IRLZ44N = MOSFET-NCHANNEL [package=to220v]
  switch = Toggle Switch [package=THT]

nets:
  GND: C1.-, C2.-, Power_12v.GND, Heltec_WiFi_LoRa_32.pin_18, Heltec_WiFi_LoRa_32.pin_19, C3.0, 7805.GND, R1.Pin_1, rotary.pin5, 12v.pin1, IRLZ44N.S
  N1: C1.+, C3.1, 7805.output_voltage, switch.COM
  N2: C2.+, Power_12v.VCC, 7805.input_voltage, tira_de_leds.pin1, 12v.pin2
  N3: Heltec_WiFi_LoRa_32.pin_11, Driver_Motor.pin1
  N4: Heltec_WiFi_LoRa_32.pin_12, Driver_Motor.pin2
  N5: Heltec_WiFi_LoRa_32.pin_13, Driver_Motor.pin3
  N6: Heltec_WiFi_LoRa_32.pin_14, Driver_Motor.pin4
  N7: Heltec_WiFi_LoRa_32.pin_15, R1.Pin_0, IRLZ44N.G
  N8: Heltec_WiFi_LoRa_32.pin_16, Heltec_WiFi_LoRa_32.pin_21, Heltec_WiFi_LoRa_32.pin_22, rotary.pin4
  N9: Heltec_WiFi_LoRa_32.pin_20, switch.L1
  N10: Heltec_WiFi_LoRa_32.pin_29, rotary.pin3
  N11: Heltec_WiFi_LoRa_32.pin_33, rotary.pin2
  N12: Heltec_WiFi_LoRa_32.pin_35, rotary.pin1
  N13: tira_de_leds.pin2, IRLZ44N.D

notes:
  +  -
  -+

custom parts:
  Heltec WiFi LoRa 32 V2: Heltec WiFi LoRa 32 V2 WiFi LoRa 32 is a classic IoT dev-board designed & produced by Heltec Automation(TM). It’s a highly integrated product based on ESP32 + SX127x, it has Wi-Fi, BLE, LoRa functions, also Li-Po battery management system, 0.96″ OLED are also included. It’s the best choice for smart cities, smart farms, smart home, and IoT makers.
  Rotary Encoder with switch (KY-040): A Rotary Encoder with switch
